// Logisim project 8bit.circ as structural Verilog: 6 circuits, main circuit cpu
module cpu (
  input  RESET,
  output [7:0] GPIOS
);

  wire alu_1_out_6, alu_1_out_7, alu_1_out_8, aludecode_1_aluen, aludecode_1_flags, aludecode_1_jen,
       aludecode_1_mem_r, aludecode_1_op1en, aludecode_1_out_18, aludecode_1_out_19, aludecode_1_rden,
       aludecode_1_rel_abs, aludecode_1_rnen, aludecode_1_u_cond, aludecode_1_z_c, and_1_out, and_2_out,
       and_3_out, and_4_out, and_5_out, and_6_out, and_7_out, and_8_out, and_9_out, and_10_out, and_11_out,
       clock_1_out, comparator_1_eq, not_1_out, not_2_out, or_1_out, or_2_out, or_3_out, or_4_out,
       register_2_q, register_3_q, xor_1_out;
  wire [1:0] priority_encoder_1_out, priority_encoder_2_out, priority_encoder_3_out, priority_encoder_4_out,
       priority_encoder_5_out;
  wire [2:0] aludecode_1_rd, aludecode_1_rn;
  wire [3:0] aludecode_1_opcode;
  wire [7:0] alu_1_out_9, aludecode_1_out_10, aludecode_1_out_11, multiplexer_1_out, multiplexer_2_out,
       multiplexer_3_out, multiplexer_4_out, multiplexer_5_out, pc_block_1_out_7, ram_1_data,
       regfile_1_out_7, regfile_1_out_8;
  wire [15:0] rom_1_data;

  LED led_1 (.in(GPIOS[0]));
  LED led_2 (.in(GPIOS[1]));
  LED led_3 (.in(GPIOS[2]));
  LED led_4 (.in(GPIOS[3]));
  LED led_5 (.in(GPIOS[4]));
  LED led_6 (.in(GPIOS[5]));
  LED led_7 (.in(GPIOS[6]));
  LED led_8 (.in(GPIOS[7]));
  Register register_1 (.D(multiplexer_2_out), .en(1'b1), .Q(GPIOS), .clk(and_1_out), .clr(RESET));
  and and_1 (and_1_out, comparator_1_eq, clock_1_out);
  Comparator #(.mode("unsigned")) comparator_1 (
    .a(multiplexer_1_out), .b({8{1'b0}}), .eq(comparator_1_eq));  // open: gt, lt
  or or_1 (or_1_out, and_2_out, and_3_out, and_6_out);
  xor xor_1 (xor_1_out, aludecode_1_mem_r, or_1_out);
  and and_2 (and_2_out, register_3_q, aludecode_1_z_c, and_5_out);
  and and_3 (and_3_out, and_5_out, ~aludecode_1_z_c, register_2_q);  // AND_Gate
  and and_4 (and_4_out, xor_1_out, aludecode_1_jen);
  not not_1 (not_1_out, clock_1_out);
  Clock clock_1 (.out(clock_1_out));
  pc_block pc_block_1 (
    .in_1(aludecode_1_out_11), .in_2(and_4_out), .in_3(aludecode_1_out_11), .in_4(aludecode_1_rel_abs),
    .in_5(not_1_out), .out_7(pc_block_1_out_7), .in_6(RESET));
  Multiplexer #(.select(2), .width(8), .disabled(0), .enable("false")) multiplexer_1 (
    .in0(aludecode_1_out_10), .in1(regfile_1_out_8), .out(multiplexer_1_out), .sel(priority_encoder_1_out));  // open: in2, in3
  Priority_Encoder #(.select(2), .disabled(0)) priority_encoder_1 (
    .in0(and_7_out), .in1(and_8_out), .out(priority_encoder_1_out));  // open: in2, in3, gs, en_out, en_in
  Multiplexer #(.select(2), .width(8), .disabled(0), .enable("false")) multiplexer_2 (
    .in0(alu_1_out_9), .in1(alu_1_out_9), .out(multiplexer_2_out), .sel(priority_encoder_2_out));  // open: in2, in3
  Priority_Encoder #(.select(2), .disabled(0)) priority_encoder_2 (
    .in0(and_7_out), .in1(and_8_out), .out(priority_encoder_2_out));  // open: in2, in3, gs, en_out, en_in
  and and_5 (and_5_out, aludecode_1_u_cond, aludecode_1_jen);
  and and_6 (and_6_out, ~aludecode_1_u_cond, aludecode_1_jen);  // AND_Gate
  or or_2 (or_2_out, and_8_out, and_7_out);
  ROM #(.dataWidth(16)) rom_1 (.addr(pc_block_1_out_7), .data(rom_1_data), .sel(1'b1));
  RAM #(.bus("separate")) ram_1 (
    .addr(multiplexer_1_out), .din(multiplexer_2_out), .data(ram_1_data), .str(or_2_out), .sel(1'b1),
    .clk(clock_1_out), .ld(1'b1), .clr(RESET));
  aludecode aludecode_1 (
    .in_1(rom_1_data), .aluen(aludecode_1_aluen), .rel_abs(aludecode_1_rel_abs), .u_cond(aludecode_1_u_cond),
    .z_c(aludecode_1_z_c), .mem_r(aludecode_1_mem_r), .jen(aludecode_1_jen), .op1en(aludecode_1_op1en),
    .out_10(aludecode_1_out_10), .out_11(aludecode_1_out_11), .rn(aludecode_1_rn), .rd(aludecode_1_rd),
    .rnen(aludecode_1_rnen), .rden(aludecode_1_rden), .flags(aludecode_1_flags), .opcode(aludecode_1_opcode),
    .out_18(aludecode_1_out_18), .out_19(aludecode_1_out_19));  // open: op2en
  and and_7 (and_7_out, or_3_out, aludecode_1_op1en);
  and and_8 (and_8_out, or_3_out, aludecode_1_rnen);
  not not_2 (not_2_out, or_3_out);
  and and_9 (and_9_out, aludecode_1_aluen, clock_1_out);
  Multiplexer #(.select(2), .width(8), .disabled(0), .enable("false")) multiplexer_3 (
    .in0(alu_1_out_9), .out(multiplexer_3_out), .sel(priority_encoder_3_out));  // open: in1, in2, in3
  Priority_Encoder #(.select(2), .disabled(0)) priority_encoder_3 (
    .in0(not_2_out), .out(priority_encoder_3_out));  // open: in1, in2, in3, gs, en_out, en_in
  regfile regfile_1 (
    .in_1(multiplexer_3_out), .in_2(and_9_out), .in_3(aludecode_1_rn), .in_4(not_2_out),
    .in_5(aludecode_1_rd), .out_7(regfile_1_out_7), .out_8(regfile_1_out_8), .in_6(RESET));
  or or_3 (or_3_out, aludecode_1_out_19, alu_1_out_8);
  or or_4 (or_4_out, aludecode_1_out_18, aludecode_1_out_18);
  and and_10 (and_10_out, or_4_out, aludecode_1_rnen);
  Priority_Encoder #(.select(2), .disabled(0)) priority_encoder_4 (
    .in0(1'b1), .in1(aludecode_1_rden), .in2(alu_1_out_8), .in3(aludecode_1_out_19),
    .out(priority_encoder_4_out));  // open: gs, en_out, en_in
  Priority_Encoder #(.select(2), .disabled(0)) priority_encoder_5 (
    .in0(1'b1), .in1(aludecode_1_rnen), .in2(aludecode_1_op1en), .in3(and_10_out),
    .out(priority_encoder_5_out));  // open: gs, en_out, en_in
  and and_11 (and_11_out, clock_1_out, aludecode_1_flags);
  Multiplexer #(.select(2), .width(8), .disabled(0), .enable("false")) multiplexer_4 (
    .in0({8{1'b0}}), .in1(regfile_1_out_8), .in2(regfile_1_out_8), .in3(ram_1_data), .out(multiplexer_4_out),
    .sel(priority_encoder_4_out));
  Multiplexer #(.select(2), .width(8), .disabled(0), .enable("false")) multiplexer_5 (
    .in0({8{1'b0}}), .in1(regfile_1_out_7), .in2(aludecode_1_out_10), .in3(ram_1_data),
    .out(multiplexer_5_out), .sel(priority_encoder_5_out));
  alu alu_1 (
    .in_1(register_2_q), .in_2(register_3_q), .in_3(multiplexer_4_out), .in_4(multiplexer_5_out),
    .in_5(aludecode_1_opcode), .out_6(alu_1_out_6), .out_7(alu_1_out_7), .out_8(alu_1_out_8),
    .out_9(alu_1_out_9));
  Register #(.width(1)) register_2 (.D(alu_1_out_7), .Q(register_2_q), .clk(and_11_out));  // open: en, clr
  Register #(.width(1)) register_3 (.D(alu_1_out_6), .Q(register_3_q), .clk(and_11_out));  // open: en, clr

  // Notes on the sheet:
  //   GPIOS: pull=down
  //   RESET: pull=down
  //   contents of rom_1 (hex, n*v repeats v):
  //   b801 ba42 ac02 ef51 ef49 bb2a ac02 ef51 ef59 bb62 ac02 ef51 ef59 bb62 ac02 ef51 ef59 bb7a ac02 ef51
  //   c0ff
endmodule

module regfile (
  input  [7:0] in_1,
  input  in_2,
  input  [2:0] in_3,
  input  in_4,
  input  [2:0] in_5,
  input  in_6,
  output [7:0] out_7,
  output [7:0] out_8
);

  wire decoder_1_out0, decoder_1_out1, decoder_1_out2, decoder_1_out3, decoder_1_out4, decoder_1_out5,
       decoder_1_out6, decoder_1_out7;
  wire [7:0] register_1_q, register_2_q, register_3_q, register_4_q, register_5_q, register_6_q,
       register_7_q, register_8_q;

  Decoder #(.select(3), .disabled(0)) decoder_1 (
    .out0(decoder_1_out0), .out1(decoder_1_out1), .out2(decoder_1_out2), .out3(decoder_1_out3),
    .out4(decoder_1_out4), .out5(decoder_1_out5), .out6(decoder_1_out6), .out7(decoder_1_out7), .sel(in_5),
    .en(in_4));
  Register register_1 (.D(in_1), .en(decoder_1_out0), .Q(register_1_q), .clk(in_2), .clr(in_6));
  Register register_2 (.D(in_1), .en(decoder_1_out1), .Q(register_2_q), .clk(in_2), .clr(in_6));
  Register register_3 (.D(in_1), .en(decoder_1_out2), .Q(register_3_q), .clk(in_2), .clr(in_6));
  Register register_4 (.D(in_1), .en(decoder_1_out3), .Q(register_4_q), .clk(in_2), .clr(in_6));
  Register register_5 (.D(in_1), .en(decoder_1_out4), .Q(register_5_q), .clk(in_2), .clr(in_6));
  Register register_6 (.D(in_1), .en(decoder_1_out5), .Q(register_6_q), .clk(in_2), .clr(in_6));
  Register register_7 (.D(in_1), .en(decoder_1_out6), .Q(register_7_q), .clk(in_2), .clr(in_6));
  Register register_8 (.D(in_1), .en(decoder_1_out7), .Q(register_8_q), .clk(in_2), .clr(in_6));
  Multiplexer #(.select(3), .width(8), .disabled(0), .enable("false")) multiplexer_1 (
    .in0(register_1_q), .in1(register_2_q), .in2(register_3_q), .in3(register_4_q), .in4(register_5_q),
    .in5(register_6_q), .in6(register_7_q), .in7(register_8_q), .out(out_7), .sel(in_3));
  Multiplexer #(.select(3), .width(8), .disabled(0), .enable("false")) multiplexer_2 (
    .in0(register_1_q), .in1(register_2_q), .in2(register_3_q), .in3(register_4_q), .in4(register_5_q),
    .in5(register_6_q), .in6(register_7_q), .in7(register_8_q), .out(out_8), .sel(in_5));
endmodule

module pc_block (
  input  [7:0] in_1,
  input  in_2,
  input  [7:0] in_3,
  input  in_4,
  input  in_5,
  input  in_6,
  output [7:0] out_7
);

  wire and_1_out, and_2_out;
  wire [7:0] adder_1_out, multiplexer_1_out, multiplexer_2_out;

  and and_1 (and_1_out, in_2, ~in_4);  // AND_Gate
  Multiplexer #(.width(8), .disabled(0), .enable("false")) multiplexer_1 (
    .in0({8{1'b0}}), .in1(in_1), .out(multiplexer_1_out), .sel(and_1_out));
  Adder adder_1 (.a(out_7), .b(multiplexer_1_out), .out(adder_1_out), .cin(1'b1));  // open: cout
  and and_2 (and_2_out, in_2, in_4);
  Multiplexer #(.width(8), .disabled(0), .enable("false")) multiplexer_2 (
    .in0(adder_1_out), .in1(in_3), .out(multiplexer_2_out), .sel(and_2_out));
  Register register_1 (.D(multiplexer_2_out), .en(1'b1), .Q(out_7), .clk(in_5), .clr(in_6));
endmodule

module aludecode (
  input  [15:0] in_1,
  output aluen,
  output rel_abs,
  output u_cond,
  output z_c,
  output mem_r,
  output jen,
  output op1en,
  output op2en,
  output [7:0] out_10,
  output [7:0] out_11,
  output [2:0] rn,
  output [2:0] rd,
  output rnen,
  output rden,
  output flags,
  output [3:0] opcode,
  output out_18,
  output out_19
);

  wire and_2_out, and_3_out, and_4_out, and_6_out, not_1_out, not_2_out;

  nand nand_1 (op1en, in_1[15], in_1[14]);
  not not_1 (not_1_out, op1en);
  and and_1 (jen, ~in_1[13], not_1_out);  // AND_Gate
  and and_2 (and_2_out, in_1[13], not_1_out);
  and and_3 (and_3_out, rnen, aluen);
  Multiplexer #(.width(4), .disabled(0), .enable("false")) multiplexer_1 (
    .in0(4'b0000), .in1(in_1[12:9]), .out({rel_abs, u_cond, z_c, mem_r}), .sel(jen));
  and and_4 (and_4_out, aluen, op1en);
  and and_5 (out_18, and_3_out, in_1[7]);
  or or_1 (rnen, jen, and_2_out);
  or or_2 (flags, op1en, and_6_out);
  and and_6 (and_6_out, and_2_out, in_1[8]);
  and and_7 (out_19, and_3_out, in_1[6]);
  not not_2 (not_2_out, op1en);
  or or_3 (aluen, op1en, and_2_out);
  Multiplexer #(.width(4), .disabled(0)) multiplexer_2 (
    .in0(in_1[14:11]), .in1(in_1[12:9]), .out(opcode), .sel(not_2_out), .en(aluen));

  assign op2en = jen;
  assign out_10 = in_1[10:3];
  assign out_11 = in_1[7:0];
  assign rd = in_1[2:0];
  assign rden = aluen;
  assign rn = in_1[5:3];

  // Notes on the sheet:
  //   aluimm
  //   jmpimm
endmodule

module alu (
  input  in_1,
  input  in_2,
  input  [7:0] in_3,
  input  [7:0] in_4,
  input  [3:0] in_5,
  output out_6,
  output out_7,
  output out_8,
  output [7:0] out_9
);

  wire adder_1_cout, and_1_out, and_2_out, and_3_out, and_5_out, comparator_1_gt, comparator_2_eq,
       comparator_2_lt, comparator_3_eq, comparator_5_eq, decoder_1_out4, decoder_1_out5, decoder_1_out6,
       or_2_out, or_3_out, or_4_out, subtractor_1_bout;
  wire [3:0] bitadder_1_out;
  wire [7:0] adder_1_out, adder_2_out, and_4_out, divider_1_out, multiplier_1_cout, multiplier_1_out,
       or_1_out, shifter_1_out, shifter_2_out, shifter_3_out, subtractor_1_out, xor_1_out;

  Multiplier multiplier_1 (.a(in_3), .b(in_4), .out(multiplier_1_out), .cout(multiplier_1_cout));  // open: cin
  and and_1 (and_1_out, in_2, decoder_1_out4);
  Adder adder_1 (.a(in_3), .b(in_4), .out(adder_1_out), .cin(and_1_out), .cout(adder_1_cout));
  and and_2 (and_2_out, in_2, decoder_1_out4);
  BitAdder bitadder_1 (.in0(multiplier_1_cout), .out(bitadder_1_out));
  and and_3 (and_3_out, in_2, decoder_1_out6);
  Adder adder_2 (.a(in_3), .b({8{1'b0}}), .out(adder_2_out), .cin(and_3_out));  // open: cout
  Subtractor subtractor_1 (.a(in_3), .b(in_4), .out(subtractor_1_out), .bin(and_2_out), .bout(subtractor_1_bout));
  Comparator #(.width(4), .mode("unsigned")) comparator_1 (
    .a(bitadder_1_out), .b(4'b0000), .gt(comparator_1_gt));  // open: eq, lt
  Divider divider_1 (.a(in_3), .b(in_4), .out(divider_1_out));  // open: upper, rem
  assign and_4_out = in_3 & in_4;  // AND_Gate and_4, 8 bits wide
  assign or_1_out = in_3 | in_4;  // OR_Gate or_1, 8 bits wide
  assign xor_1_out = in_3 ^ in_4;  // XOR_Gate xor_1, 8 bits wide
  Comparator #(.mode("unsigned")) comparator_2 (
    .a(adder_2_out), .b(in_4), .eq(comparator_2_eq), .lt(comparator_2_lt));  // open: gt
  Shifter shifter_1 (.in(in_3), .\dist (in_4[2:0]), .out(shifter_1_out));
  Shifter #(.shift("lr")) shifter_2 (.in(in_3), .\dist (in_4[2:0]), .out(shifter_2_out));
  Shifter #(.shift("ar")) shifter_3 (.in(in_3), .\dist (in_4[2:0]), .out(shifter_3_out));
  Comparator #(.width(4), .mode("unsigned")) comparator_3 (
    .a(in_5), .b(4'b0111), .eq(comparator_3_eq));  // open: gt, lt
  Comparator #(.width(4), .mode("unsigned")) comparator_4 (.a(in_5), .b(4'b1010), .eq(out_8));  // open: gt, lt
  Multiplexer #(.select(4), .disabled(0), .enable("false")) multiplexer_1 (
    .in0(adder_1_cout), .in1(subtractor_1_bout), .in2(comparator_1_gt), .in3(in_2), .in4(in_2), .in5(in_2),
    .in6(in_2), .in7(in_2), .in8(adder_1_cout), .in9(subtractor_1_bout), .in10(in_2), .in11(comparator_2_lt),
    .in12(comparator_2_lt), .in13(in_2), .in14(in_2), .in15(in_2), .out(out_6), .sel(in_5));
  Multiplexer #(.select(4), .width(8), .disabled(0), .enable("false")) multiplexer_2 (
    .in0(adder_1_out), .in1(subtractor_1_out), .in2(multiplier_1_out), .in3(divider_1_out), .in4(and_4_out),
    .in5(or_1_out), .in6(xor_1_out), .in7(in_4), .in8(adder_1_out), .in9(subtractor_1_out), .in10(in_3),
    .in11(in_3), .in12(in_3), .in13(shifter_1_out), .in14(shifter_2_out), .in15(shifter_3_out), .out(out_9),
    .sel(in_5));
  Comparator #(.mode("unsigned")) comparator_5 (.a(out_9), .b({8{1'b0}}), .eq(comparator_5_eq));  // open: gt, lt
  or or_2 (or_2_out, decoder_1_out6, decoder_1_out5);
  and and_5 (and_5_out, comparator_2_eq, or_2_out);
  Decoder #(.select(3), .disabled(0), .enable("false")) decoder_1 (
    .out4(decoder_1_out4), .out5(decoder_1_out5), .out6(decoder_1_out6), .sel(in_5[3:1]));  // open: out0, out1, out2, out3, out7
  or or_3 (or_3_out, comparator_3_eq, out_8);
  or or_4 (or_4_out, comparator_5_eq, and_5_out);
  Multiplexer #(.disabled(0), .enable("false")) multiplexer_3 (.in0(or_4_out), .in1(in_1), .out(out_7), .sel(or_3_out));
endmodule

module test_cpu (
);

  wire pull_resistor_1_node, pull_resistor_2_node;
  wire [7:0] cpu_1_gpios;

  Pull_Resistor pull_resistor_1 (.node(pull_resistor_1_node));
  cpu cpu_1 (.RESET(pull_resistor_1_node), .GPIOS(cpu_1_gpios));
  TTY tty_1 (.data(cpu_1_gpios[6:0]), .clk(cpu_1_gpios[7]), .we(1'b1), .clr(pull_resistor_2_node));
  Pull_Resistor pull_resistor_2 (.node(pull_resistor_2_node));
  // also tied to GND on the sheet: pull_resistor_2_node
endmodule
